# Fritzing sketch Kinesis (saved by Fritzing 0.9.3b)
breadboards: 1

parts:
  Part1 = Arduino Pro Mini v13
  R1 = Basic Flex Resistor
  R2 = Basic Flex Resistor
  R3 = Basic Flex Resistor
  R4 = Resistor [tolerance=±5% resistance=10k package="2010 [SMD]"]
  R5 = Resistor [tolerance=±5% resistance=10k package="2010 [SMD]"]
  R6 = Resistor [tolerance=±5% resistance=10k package="2010 [SMD]"]
  Part2 = Triple Axis Gyro Breakout ITG-3200

nets:
  VCC: Part1.VCC, R1.pin_1, R2.pin_1, R3.pin_1, Part2.VCC
  GND: Part1.GND, R4.Pin_1, R5.Pin_1, R6.Pin_1, Part2.GND
  N1: Part1.A2, R1.Pin_2, R6.Pin_0
  N2: Part1.A1, R3.Pin_2, R5.Pin_0
  N3: Part1.A0, R2.Pin_2, R4.Pin_0
  N4: Part1.D7, Part2.INT
  N5: Part1.D3_PWM, Part2.SCL
  N6: Part1.D2, Part2.SDA
